# Fritzing sketch Ethernet_Sensor_Shield (saved by Fritzing 0.9.2b)
circuit board: 5.07736cm x 5.33241cm
breadboards: 1

parts:
  DS18B20 = screw terminal, 3 pins
  DS18B20_2 = screw terminal, 3 pins
  DS18B20_3 = screw terminal, 3 pins
  5V = Header 1 [package=1x01_offset]
  GND = Header 1 [package=1x01_offset]
  OUT_D2 = Header 1 [package=1x01_offset]
  3_3V = Header 1 [package=1x01_offset]
  Gnd = Header 1 [package=1x01_offset]
  SDA(A4) = Header 1 [package=1x01_offset]
  4_7k = Resistor [tolerance=±5% resistance=4.7k package=THT]
  SCL(A5) = Header 1 [package=1x01_offset]
  TS_logger_r1 = Arduino Board Ethernet

nets:
  N1: DS18B20.pin1, DS18B20_2.pin1, DS18B20_3.pin1, GND.1, Gnd.1, TS_logger_r1.GND
  N2: DS18B20.pin2, DS18B20_2.pin2, DS18B20_3.pin2, 4_7k.Pin_0, TS_logger_r1.D7
  N3: DS18B20.pin3, DS18B20_2.pin3, DS18B20_3.pin3, 5V.1, 4_7k.Pin_1, TS_logger_r1.5V
  N4: OUT_D2.1, TS_logger_r1.D2_PWM
  N5: 3_3V.1, TS_logger_r1.3V3
  N6: SDA(A4).1, TS_logger_r1.A4
  N7: SCL(A5).1, TS_logger_r1.A5

notes:
  BMP180
  Gnd  D7  5V
  5V  D7  Gnd
  DHT11
